# Fritzing sketch pcb-in-a-box (saved by Fritzing 0.7.12b)
breadboards: 1
perfboards: 10

parts:
  Arduino1 = Arduino
  LCD1 = LCD screen
  UV24 = Blue LED - 5mm
  UV23 = Blue LED - 5mm
  UV22 = Blue LED - 5mm
  UV49 = Blue LED - 5mm
  UV51 = Blue LED - 5mm
  UV50 = Blue LED - 5mm
  LED8 = LED - 5mm [color="Green (570nm)" package="5 mm [THT]"]
  S1 = Pushbutton [package="[THT]"]
  S2 = Pushbutton [package="[THT]"]
  Power_plug1 = Power plug
  Q3 = NPN-Transistor [package="TO92 [THT]"]
  R4 = Trimmer Potentiometer [maximum_resistance=10kΩ package=THT]
  R2 = Dial Potentiometer with switch [maximum_resistance=100kΩ]
  Q4 = NPN-Transistor [package="TO92 [THT]"]
  UV19 = Blue LED - 5mm
  UV20 = Blue LED - 5mm
  UV21 = Blue LED - 5mm
  UV52 = Blue LED - 5mm
  UV17 = Blue LED - 5mm
  UV18 = Blue LED - 5mm
  UV54 = Blue LED - 5mm
  UV55 = Blue LED - 5mm
  UV53 = Blue LED - 5mm
  UV56 = Blue LED - 5mm
  Q5 = NPN-Transistor [package="TO92 [THT]"]
  Q6 = NPN-Transistor [package="TO92 [THT]"]
  Q7 = NPN-Transistor [package="TO92 [THT]"]
  Q8 = NPN-Transistor [package="TO92 [THT]"]
  UV58 = Blue LED - 5mm
  UV62 = Blue LED - 5mm
  UV59 = Blue LED - 5mm
  UV63 = Blue LED - 5mm
  UV57 = Blue LED - 5mm
  UV61 = Blue LED - 5mm
  UV60 = Blue LED - 5mm
  UV64 = Blue LED - 5mm
  UV29 = Blue LED - 5mm
  UV27 = Blue LED - 5mm
  UV32 = Blue LED - 5mm
  UV28 = Blue LED - 5mm
  UV26 = Blue LED - 5mm
  UV25 = Blue LED - 5mm
  UV30 = Blue LED - 5mm
  UV31 = Blue LED - 5mm
  UV42 = Blue LED - 5mm
  UV46 = Blue LED - 5mm
  UV43 = Blue LED - 5mm
  UV47 = Blue LED - 5mm
  UV41 = Blue LED - 5mm
  UV45 = Blue LED - 5mm
  UV44 = Blue LED - 5mm
  UV48 = Blue LED - 5mm
  UV05 = Blue LED - 5mm
  UV03 = Blue LED - 5mm
  UV08 = Blue LED - 5mm
  UV04 = Blue LED - 5mm
  UV02 = Blue LED - 5mm
  UV01 = Blue LED - 5mm
  UV06 = Blue LED - 5mm
  UV07 = Blue LED - 5mm
  R1 = Dial Potentiometer with switch [maximum_resistance=100kΩ]
  UV34 = Blue LED - 5mm
  UV38 = Blue LED - 5mm
  UV35 = Blue LED - 5mm
  UV39 = Blue LED - 5mm
  UV33 = Blue LED - 5mm
  UV37 = Blue LED - 5mm
  UV40 = Blue LED - 5mm
  UV13 = Blue LED - 5mm
  UV11 = Blue LED - 5mm
  UV16 = Blue LED - 5mm
  UV12 = Blue LED - 5mm
  UV10 = Blue LED - 5mm
  UV09 = Blue LED - 5mm
  UV14 = Blue LED - 5mm
  UV15 = Blue LED - 5mm
  Q9 = NPN-Transistor [package="TO92 [THT]"]
  Q10 = NPN-Transistor [package="TO92 [THT]"]
  R81 = Resistor [tolerance=±5% resistance=150 package=THT]
  R82 = Resistor [tolerance=±5% resistance=150 package=THT]
  R83 = Resistor [tolerance=±5% resistance=680 package=THT]
  R84 = Resistor [tolerance=±5% resistance=680 package=THT]
  R85 = Resistor [tolerance=±5% resistance=680 package=THT]
  R86 = Resistor [tolerance=±5% resistance=680 package=THT]
  R87 = Resistor [tolerance=±5% resistance=680 package=THT]
  R88 = Resistor [tolerance=±5% resistance=680 package=THT]
  R89 = Resistor [tolerance=±5% resistance=680 package=THT]
  R90 = Resistor [tolerance=±5% resistance=680 package=THT]
  R91 = Resistor [tolerance=±5% resistance=680 package=THT]
  R92 = Resistor [tolerance=±5% resistance=680 package=THT]
  R93 = Resistor [tolerance=±5% resistance=680 package=THT]
  R94 = Resistor [tolerance=±5% resistance=680 package=THT]
  R95 = Resistor [tolerance=±5% resistance=680 package=THT]
  R96 = Resistor [tolerance=±5% resistance=680 package=THT]
  R97 = Resistor [tolerance=±5% resistance=680 package=THT]
  R98 = Resistor [tolerance=±5% resistance=680 package=THT]
  R99 = Resistor [tolerance=±5% resistance=680 package=THT]
  R100 = Resistor [tolerance=±5% resistance=680 package=THT]
  R101 = Resistor [tolerance=±5% resistance=680 package=THT]
  R102 = Resistor [tolerance=±5% resistance=680 package=THT]
  R103 = Resistor [tolerance=±5% resistance=680 package=THT]
  R104 = Resistor [tolerance=±5% resistance=680 package=THT]
  R105 = Resistor [tolerance=±5% resistance=680 package=THT]
  R106 = Resistor [tolerance=±5% resistance=680 package=THT]
  R107 = Resistor [tolerance=±5% resistance=680 package=THT]
  R108 = Resistor [tolerance=±5% resistance=680 package=THT]
  R109 = Resistor [tolerance=±5% resistance=680 package=THT]
  R110 = Resistor [tolerance=±5% resistance=680 package=THT]
  R111 = Resistor [tolerance=±5% resistance=680 package=THT]
  R112 = Resistor [tolerance=±5% resistance=680 package=THT]
  R113 = Resistor [tolerance=±5% resistance=680 package=THT]
  R114 = Resistor [tolerance=±5% resistance=680 package=THT]
  R115 = Resistor [tolerance=±5% resistance=680 package=THT]
  R116 = Resistor [tolerance=±5% resistance=680 package=THT]
  R117 = Resistor [tolerance=±5% resistance=680 package=THT]
  R118 = Resistor [tolerance=±5% resistance=680 package=THT]
  R119 = Resistor [tolerance=±5% resistance=680 package=THT]
  R120 = Resistor [tolerance=±5% resistance=680 package=THT]
  R121 = Resistor [tolerance=±5% resistance=680 package=THT]
  R122 = Resistor [tolerance=±5% resistance=680 package=THT]
  R123 = Resistor [tolerance=±5% resistance=680 package=THT]
  R124 = Resistor [tolerance=±5% resistance=680 package=THT]
  R125 = Resistor [tolerance=±5% resistance=680 package=THT]
  R126 = Resistor [tolerance=±5% resistance=680 package=THT]
  R127 = Resistor [tolerance=±5% resistance=680 package=THT]
  R128 = Resistor [tolerance=±5% resistance=680 package=THT]
  R129 = Resistor [tolerance=±5% resistance=680 package=THT]
  R130 = Resistor [tolerance=±5% resistance=680 package=THT]
  LED7 = LED - 5mm [color="Red (633nm)" package="5 mm [THT]"]
  R131 = Resistor [tolerance=±5% resistance=1k package=THT]
  R132 = Resistor [tolerance=±5% resistance=1k package=THT]
  R133 = Resistor [tolerance=±5% resistance=1k package=THT]
  R134 = Resistor [tolerance=±5% resistance=1k package=THT]
  R135 = Resistor [tolerance=±5% resistance=1k package=THT]
  R136 = Resistor [tolerance=±5% resistance=1k package=THT]
  R137 = Resistor [tolerance=±5% resistance=1k package=THT]
  R138 = Resistor [tolerance=±5% resistance=1k package=THT]
  R139 = Resistor [tolerance=±5% resistance=680 package=THT]
  R140 = Resistor [tolerance=±5% resistance=680 package=THT]
  R141 = Resistor [tolerance=±5% resistance=680 package=THT]
  R142 = Resistor [tolerance=±5% resistance=680 package=THT]
  R143 = Resistor [tolerance=±5% resistance=680 package=THT]
  R144 = Resistor [tolerance=±5% resistance=680 package=THT]
  R145 = Resistor [tolerance=±5% resistance=680 package=THT]
  R146 = Resistor [tolerance=±5% resistance=680 package=THT]
  R147 = Resistor [tolerance=±5% resistance=680 package=THT]
  R148 = Resistor [tolerance=±5% resistance=680 package=THT]
  R149 = Resistor [tolerance=±5% resistance=680 package=THT]
  R150 = Resistor [tolerance=±5% resistance=680 package=THT]
  R151 = Resistor [tolerance=±5% resistance=680 package=THT]
  R152 = Resistor [tolerance=±5% resistance=680 package=THT]
  R153 = Resistor [tolerance=±5% resistance=680 package=THT]
  R154 = Resistor [tolerance=±5% resistance=680 package=THT]
  J1 = shrouded pin header, 10 pins [form="♂ (shrouded male)"]
  J2 = shrouded pin header, 10 pins [form="♂ (shrouded male)"]
  J3 = shrouded pin header, 10 pins [form="♂ (shrouded male)"]
  J4 = shrouded pin header, 10 pins [form="♂ (shrouded male)"]
  S3 = Pushbutton [package="[THT]"]
  J5 = male pin header, 3 pins [form="♂ (male)"]
  J6 = male pin header, 3 pins [form="♂ (male)"]
  UV36 = Blue LED - 5mm

nets:
  GND: Arduino1.GND, LCD1.VSS, LCD1.R/W, LCD1.LED-, LED8.cathode, S1.Pin_1, S1.Pin_2, S2.Pin_1, S2.Pin_2, Power_plug1.GND, Q3.E, R4.leg2, R2.leg2, Q4.E, Q5.E, Q6.E, Q7.E, Q8.E, R1.leg1, Q9.E, Q10.E, LED7.cathode, J1.pin5, J1.pin6, J2.pin5, J2.pin6, J3.pin5, J3.pin6, J4.pin5, J4.pin6, S3.Pin_1, S3.Pin_2
  N1: Arduino1.D13, S1.Pin_3, S1.Pin_4
  N2: Arduino1.D12, R82.Pin_0
  N3: Arduino1.D11, R81.Pin_0
  N4: Arduino1.D10, R131.Pin_1, R132.Pin_1, R133.Pin_1, R134.Pin_1, J1.pin2, J1.pin9, J6.pin2
  N5: Arduino1.D9, R135.Pin_1, R136.Pin_1, R137.Pin_1, R138.Pin_1, J1.pin4, J1.pin7, J5.pin2
  N6: Arduino1.D8, S2.Pin_3, S2.Pin_4
  N7: Arduino1.D7, LCD1.RS
  N8: Arduino1.D6, LCD1.E
  N9: Arduino1.D5, LCD1.DB4
  N10: Arduino1.D4, LCD1.DB5
  N11: Arduino1.D3, LCD1.DB6
  N12: Arduino1.D2, LCD1.DB7
  N13: Arduino1.RST, S3.Pin_3, S3.Pin_4
  5V: Arduino1.+5V, LCD1.VDD, LCD1.LED+, R4.leg1, R2.leg1, R1.leg2
  N14: Arduino1.A0, R1.wiper
  N15: Arduino1.A1, R2.wiper
  N16: LCD1.V0, R4.wiper
  N17: UV24.cathode, UV23.cathode, UV22.cathode, UV19.cathode, UV20.cathode, UV21.cathode, UV17.cathode, UV18.cathode, Q8.C
  N18: UV24.anode, R91.Pin_1
  N19: UV23.anode, R93.Pin_1
  N20: UV22.anode, R95.Pin_1
  N21: UV49.cathode, UV51.cathode, UV50.cathode, Q3.C, UV52.cathode, UV54.cathode, UV55.cathode, UV53.cathode, UV56.cathode
  N22: UV49.anode, R121.Pin_1
  N23: UV51.anode, R118.Pin_1
  N24: UV50.anode, R115.Pin_1
  N25: LED8.anode, R81.Pin_1
  N26: Power_plug1.VCC, R83.Pin_0, R84.Pin_0, R85.Pin_0, R86.Pin_0, R87.Pin_0, R88.Pin_0, R89.Pin_0, R90.Pin_0, R91.Pin_0, R92.Pin_0, R93.Pin_0, R94.Pin_0, R95.Pin_0, R96.Pin_0, R97.Pin_0, R98.Pin_0, R99.Pin_0, R100.Pin_0, R101.Pin_0, R102.Pin_0, R103.Pin_0, R104.Pin_0, R105.Pin_0, R106.Pin_0, R107.Pin_0, R108.Pin_0, R109.Pin_0, R110.Pin_0, R111.Pin_0, R112.Pin_0, R113.Pin_0, R114.Pin_0, R115.Pin_0, R116.Pin_0, R117.Pin_0, R118.Pin_0, R119.Pin_0, R120.Pin_0, R121.Pin_0, R122.Pin_0, R123.Pin_0, R124.Pin_0, R125.Pin_0, R126.Pin_0, R127.Pin_0, R128.Pin_0, R129.Pin_0, R130.Pin_0, R139.Pin_0, R140.Pin_0, R141.Pin_0, R142.Pin_0, R143.Pin_0, R144.Pin_0, R145.Pin_0, R146.Pin_0, R147.Pin_0, R148.Pin_0, R149.Pin_0, R150.Pin_0, R151.Pin_0, R152.Pin_0, R153.Pin_0, R154.Pin_0, J1.pin1, J1.pin10, J2.pin1, J2.pin10, J3.pin1, J3.pin10, J4.pin1, J4.pin10
  N27: Q3.B, R136.Pin_0
  N28: Q4.B, R138.Pin_0
  N29: Q4.C, UV42.cathode, UV46.cathode, UV43.cathode, UV47.cathode, UV41.cathode, UV45.cathode, UV44.cathode, UV48.cathode
  N30: UV19.anode, R96.Pin_1
  N31: UV20.anode, R98.Pin_1
  N32: UV21.anode, R92.Pin_1
  N33: UV52.anode, R117.Pin_1
  N34: UV17.anode, R94.Pin_1
  N35: UV18.anode, R97.Pin_1
  N36: UV54.anode, R119.Pin_1
  N37: UV55.anode, R116.Pin_1
  N38: UV53.anode, R122.Pin_1
  N39: UV56.anode, R120.Pin_1
  N40: Q5.B, R137.Pin_0
  N41: Q5.C, UV58.cathode, UV62.cathode, UV59.cathode, UV63.cathode, UV57.cathode, UV61.cathode, UV60.cathode, UV64.cathode
  N42: Q6.B, R133.Pin_0
  N43: Q6.C, UV05.cathode, UV03.cathode, UV08.cathode, UV04.cathode, UV02.cathode, UV01.cathode, UV06.cathode, UV07.cathode
  N44: Q7.B, R132.Pin_0
  N45: Q7.C, UV29.cathode, UV27.cathode, UV32.cathode, UV28.cathode, UV26.cathode, UV25.cathode, UV30.cathode, UV31.cathode
  N46: Q8.B, R131.Pin_0
  N47: UV58.anode, R129.Pin_1
  N48: UV62.anode, R123.Pin_1
  N49: UV59.anode, R128.Pin_1
  N50: UV63.anode, R124.Pin_1
  N51: UV57.anode, R126.Pin_1
  N52: UV61.anode, R125.Pin_1
  N53: UV60.anode, R127.Pin_1
  N54: UV64.anode, R130.Pin_1
  N55: UV29.anode, R86.Pin_1
  N56: UV27.anode, R89.Pin_1
  N57: UV32.anode, R83.Pin_1
  N58: UV28.anode, R87.Pin_1
  N59: UV26.anode, R90.Pin_1
  N60: UV25.anode, R88.Pin_1
  N61: UV30.anode, R85.Pin_1
  N62: UV31.anode, R84.Pin_1
  N63: UV42.anode, R147.Pin_1
  N64: UV46.anode, R149.Pin_1
  N65: UV43.anode, R152.Pin_1
  N66: UV47.anode, R151.Pin_1
  N67: UV41.anode, R148.Pin_1
  N68: UV45.anode, R150.Pin_1
  N69: UV44.anode, R154.Pin_1
  N70: UV48.anode, R153.Pin_1
  N71: UV05.anode, R109.Pin_1
  N72: UV03.anode, R111.Pin_1
  N73: UV08.anode, R108.Pin_1
  N74: UV04.anode, R113.Pin_1
  N75: UV02.anode, R107.Pin_1
  N76: UV01.anode, R112.Pin_1
  N77: UV06.anode, R110.Pin_1
  N78: UV07.anode, R114.Pin_1
  N79: UV34.cathode, UV38.cathode, UV35.cathode, UV39.cathode, UV33.cathode, UV37.cathode, UV40.cathode, Q9.C, UV36.cathode
  N80: UV34.anode, R145.Pin_1
  N81: UV38.anode, R139.Pin_1
  N82: UV35.anode, R144.Pin_1
  N83: UV39.anode, R140.Pin_1
  N84: UV33.anode, R142.Pin_1
  N85: UV37.anode, R141.Pin_1
  N86: UV40.anode, R146.Pin_1
  N87: UV13.cathode, UV11.cathode, UV16.cathode, UV12.cathode, UV10.cathode, UV09.cathode, UV14.cathode, UV15.cathode, Q10.C
  N88: UV13.anode, R102.Pin_1
  N89: UV11.anode, R99.Pin_1
  N90: UV16.anode, R105.Pin_1
  N91: UV12.anode, R101.Pin_1
  N92: UV10.anode, R106.Pin_1
  N93: UV09.anode, R100.Pin_1
  N94: UV14.anode, R104.Pin_1
  N95: UV15.anode, R103.Pin_1
  N96: Q9.B, R135.Pin_0
  N97: Q10.B, R134.Pin_0
  N98: R82.Pin_1, LED7.anode
  N99: R143.Pin_1, UV36.anode
  N100: J2.pin2, J2.pin9, J3.pin2, J3.pin9, J5.pin1
  N101: J2.pin3, J2.pin8
  N102: J2.pin4, J2.pin7, J3.pin4, J3.pin7, J5.pin3
  N103: J3.pin3, J3.pin8
  N104: J4.pin2, J4.pin9, J6.pin1
  N105: J4.pin3, J4.pin8
  N106: J4.pin4, J4.pin7, J6.pin3

notes:
  Porque Potenciometros?
  Os Potenciomentros é uma segunda proposta substituindo os botões que selecionam a intencidade da luz e o tempo.
  LCD
  Usado um LCD Comum
  Não temos ainda um LCD i2C
  que ajudaria a sobrar mais pinos.
  19V
  2A
  Tendo dois pwm a mais, podemos usa-los para controlarmos 4 barramentos de leds de forma independetes, ou seja dois em cima dois em baixo, porém somente temos 2 PWM livres devido o uso do LCD.
